# Fritzing sketch cat_timer (saved by Fritzing 0.9.2b)
breadboards: 1

parts:
  Part1 = Arduino Nano (Rev3.0)
  LED1 = LED - 5mm [color="Red (633nm)" package="5 mm [THT]"]  # not connected
  R1 = Resistor [tolerance=±5% resistance=10k package=THT]
  R2 = Resistor [tolerance=±5% resistance=10k package=THT]
  S2 = Round Pushbutton
  R3 = Resistor [tolerance=±5% resistance=10k package=THT]
  VCC2 = Battery block 9V

nets:
  N1: Part1.D12/MISO, S2.leg1, R3.Pin_0
  N2: R1.Pin_0, VCC2.+
  N3: R1.Pin_1, R2.Pin_0
  N4: R2.Pin_1, R3.Pin_1, VCC2.-
